# Fritzing sketch power (saved by Fritzing 0.9.3b)

parts:
  Power_plug2 = Power plug
  J11 = female pin header, 1 pin [form="♀ (female)"]
  J12 = female pin header, 1 pin [form="♀ (female)"]
  J13 = female pin header, 1 pin [form="♀ (female)"]
  J14 = female pin header, 1 pin [form="♀ (female)"]
  J15 = female pin header, 1 pin [form="♀ (female)"]
  J16 = female pin header, 1 pin [form="♀ (female)"]
  J17 = female pin header, 1 pin [form="♀ (female)"]
  J18 = female pin header, 1 pin [form="♀ (female)"]
  J19 = female pin header, 1 pin [form="♀ (female)"]
  J20 = female pin header, 1 pin [form="♀ (female)"]
  Raspberry_Pi_1 = Raspberry Pi 3 [part_number=RPI-3-V1.2]
  J21 = female pin header, 1 pin [form="♀ (female)"]
  J22 = female pin header, 1 pin [form="♀ (female)"]
  J23 = female pin header, 1 pin [form="♀ (female)"]  # not connected
  J24 = female pin header, 1 pin [form="♀ (female)"]
  J25 = female pin header, 1 pin [form="♀ (female)"]
  J26 = female pin header, 1 pin [form="♀ (female)"]
  J27 = female pin header, 1 pin [form="♀ (female)"]
  J28 = female pin header, 1 pin [form="♀ (female)"]
  J29 = female pin header, 1 pin [form="♀ (female)"]  # not connected
  J30 = female pin header, 1 pin [form="♀ (female)"]  # not connected
  J31 = female pin header, 1 pin [form="♀ (female)"]
  J32 = female pin header, 1 pin [form="♀ (female)"]
  J33 = female pin header, 1 pin [form="♀ (female)"]
  J34 = female pin header, 1 pin [form="♀ (female)"]

nets:
  N1: Power_plug2.GND, J17.pin1
  N2: Power_plug2.VCC, J13.pin1, J21.pin1
  N3: J11.pin1, Raspberry_Pi_1.3v3
  N4: J12.pin1, Raspberry_Pi_1.GPIO17
  N5: J14.pin1, J15.pin1, Raspberry_Pi_1.GND, J22.pin1, J26.pin1, J32.pin1
  N6: J16.pin1, Raspberry_Pi_1.5V, J24.pin1
  N7: J18.pin1, J19.pin1
  N8: J20.pin1, J25.pin1, J31.pin1
  N9: J27.pin1, J34.pin1
  N10: J28.pin1, J33.pin1

notes:
  power on 11 / gpio17
  24V
  5V
